# Fritzing sketch Diagram (saved by Fritzing 0.9.3b)
breadboards: 1

parts:
  RHT1 = Humidity and Temperature Sensor RHT03
  Part2 = MicroSD Card Module
  Part1 = Arduino Uno (Rev3) - ICSP

nets:
  VCC: RHT1.Vcc, Part2.VCC, Part1.5V
  N1: RHT1.Data-signal, Part1.D8
  GND: RHT1.GND_2, Part2.GND, Part1.GND
  N2: Part2.MISO, Part1.D12/MISO
  N3: Part2.MOSI, Part1.D11_PWM/MOSI
  N4: Part2.SCK, Part1.D13/SCK
  N5: Part2.CS, Part1.D10_PWM/SS
